// Logisim project Final draft design.circ as structural Verilog
module PC (
  input  [19:0] Common_Bus,
  input  in_2,
  input  in_3,
  input  in_4,
  input  in_5,
  output [19:0] OUT
);

  wire or_1_out;
  wire [13:0] adder_1_out, multiplexer_1_out;

  Multiplexer #(.width(14), .enable("false")) multiplexer_1 (
    .in0(Common_Bus[13:0]), .in1(adder_1_out), .out(multiplexer_1_out), .sel(in_4));
  Adder #(.width(14)) adder_1 (.a(14'h1), .b(OUT[13:0]), .out(adder_1_out));  // open: cin, cout
  or or_1 (or_1_out, in_4, in_3);
  Register #(.width(14)) register_1 (.D(multiplexer_1_out), .en(or_1_out), .Q(OUT[13:0]), .clk(in_5), .clr(in_2));

  assign OUT[19:14] = {6{1'b0}};
endmodule

// PC Control
module PC_control (
  input  [19:0] IR,
  input  [2:0] SC,
  input  [19:0] AC,
  input  [19:0] DR,
  input  R,
  input  FGI,
  input  FGO,
  input  E,
  output Load,
  output Increment,
  output Clear
);

  wire and_3_out, and_4_out, and_5_out, and_6_out, and_7_out, and_8_out, and_9_out, and_10_out, and_11_out,
       and_12_out, and_13_out, decoder_1_out0, decoder_1_out1, decoder_1_out2, decoder_1_out3,
       decoder_1_out4, decoder_1_out5, decoder_1_out6, decoder_1_out7, decoder_2_out0, decoder_2_out1,
       decoder_2_out2, decoder_2_out3, decoder_2_out4, decoder_2_out5, decoder_2_out6, decoder_2_out7,
       decoder_2_out8, decoder_2_out9, decoder_2_out10, decoder_2_out11, decoder_2_out12, decoder_2_out13,
       decoder_2_out14, decoder_2_out15, or_1_out, or_2_out, p, r_t;

  Decoder #(.select(3)) decoder_1 (
    .out0(decoder_1_out0), .out1(decoder_1_out1), .out2(decoder_1_out2), .out3(decoder_1_out3),
    .out4(decoder_1_out4), .out5(decoder_1_out5), .out6(decoder_1_out6), .out7(decoder_1_out7), .sel(SC));  // open: en
  Decoder #(.select(4)) decoder_2 (
    .out0(decoder_2_out0), .out1(decoder_2_out1), .out2(decoder_2_out2), .out3(decoder_2_out3),
    .out4(decoder_2_out4), .out5(decoder_2_out5), .out6(decoder_2_out6), .out7(decoder_2_out7),
    .out8(decoder_2_out8), .out9(decoder_2_out9), .out10(decoder_2_out10), .out11(decoder_2_out11),
    .out12(decoder_2_out12), .out13(decoder_2_out13), .out14(decoder_2_out14), .out15(decoder_2_out15),
    .sel(IR[17:14]));  // open: en
  and and_1 (p, decoder_1_out3, IR[19], IR[18], decoder_2_out15);
  and and_2 (r_t, decoder_2_out0, decoder_1_out3, IR[19], IR[18]);
  or or_1 (or_1_out, AC[19], AC[18], AC[17], AC[16], AC[15], AC[14], AC[13], AC[12], AC[11], AC[10], AC[8], AC[7], AC[6], AC[5], AC[4], AC[3], AC[2], AC[1], AC[0], AC[9]);
  and and_3 (and_3_out, decoder_1_out5, decoder_2_out6);
  and and_4 (and_4_out, decoder_2_out7, decoder_1_out6);
  and and_5 (and_5_out, ~R, decoder_1_out1);  // AND_Gate
  and and_6 (and_6_out, R, decoder_1_out3);
  and and_7 (and_7_out, decoder_2_out8, ~or_2_out, decoder_1_out6);  // AND_Gate
  and and_8 (and_8_out, IR[6], r_t, ~AC[19]);  // AND_Gate
  and and_9 (and_9_out, IR[5], r_t, AC[19]);
  and and_10 (and_10_out, IR[4], r_t, or_1_out);
  and and_11 (and_11_out, IR[3], r_t, E);
  and and_12 (and_12_out, IR[11], p, FGI);
  and and_13 (and_13_out, IR[10], p, FGO);
  or or_2 (or_2_out, DR[19], DR[18], DR[17], DR[16], DR[15], DR[14], DR[13], DR[12], DR[11], DR[10], DR[8], DR[7], DR[6], DR[5], DR[4], DR[3], DR[2], DR[1], DR[0], DR[9]);
  or or_3 (Load, and_3_out, and_4_out);
  or or_4 (Increment, and_5_out, and_6_out, and_7_out, and_8_out, and_9_out, and_10_out, and_11_out, and_12_out, and_13_out);
  and and_14 (Clear, R, decoder_1_out2);

  // Notes on the sheet:
  //   3x8 decoder
  //   4x8 decoder
  //   D6T5
  //   D7T6
endmodule

module AC (
  input  [19:0] ALU,
  input  Incr,
  input  Clear,
  input  Load,
  input  in_5,
  output [19:0] out_6
);

  wire or_1_out;
  wire [19:0] adder_1_out, multiplexer_1_out;

  Adder #(.width(20)) adder_1 (.a(20'h1), .b(out_6), .out(adder_1_out));  // open: cin, cout
  Multiplexer #(.width(20), .enable("false")) multiplexer_1 (
    .in0(ALU), .in1(adder_1_out), .out(multiplexer_1_out), .sel(Incr));
  or or_1 (or_1_out, Incr, Load);
  Register #(.width(20)) register_1 (.D(multiplexer_1_out), .en(or_1_out), .Q(out_6), .clk(in_5), .clr(Clear));
endmodule

module AC_control (
  input  [19:0] IR,
  input  [2:0] SC,
  output Load,
  output Clear,
  output Increment
);

  wire and_1_out, and_2_out, and_3_out, and_4_out, and_5_out, and_6_out, and_7_out, and_8_out, and_9_out,
       decoder_1_out0, decoder_1_out1, decoder_1_out2, decoder_1_out3, decoder_1_out4, decoder_1_out5,
       decoder_1_out6, decoder_1_out7, decoder_2_out0, decoder_2_out1, decoder_2_out2, decoder_2_out3,
       decoder_2_out4, decoder_2_out5, decoder_2_out6, decoder_2_out7, decoder_2_out8, decoder_2_out9,
       decoder_2_out10, decoder_2_out11, decoder_2_out12, decoder_2_out13, decoder_2_out14, decoder_2_out15,
       p, r;

  Decoder #(.select(3)) decoder_1 (
    .out0(decoder_1_out0), .out1(decoder_1_out1), .out2(decoder_1_out2), .out3(decoder_1_out3),
    .out4(decoder_1_out4), .out5(decoder_1_out5), .out6(decoder_1_out6), .out7(decoder_1_out7), .sel(SC));  // open: en
  Decoder #(.select(4)) decoder_2 (
    .out0(decoder_2_out0), .out1(decoder_2_out1), .out2(decoder_2_out2), .out3(decoder_2_out3),
    .out4(decoder_2_out4), .out5(decoder_2_out5), .out6(decoder_2_out6), .out7(decoder_2_out7),
    .out8(decoder_2_out8), .out9(decoder_2_out9), .out10(decoder_2_out10), .out11(decoder_2_out11),
    .out12(decoder_2_out12), .out13(decoder_2_out13), .out14(decoder_2_out14), .out15(decoder_2_out15),
    .sel(IR[17:14]));  // open: en
  and and_1 (and_1_out, decoder_2_out0, decoder_1_out5);
  and and_2 (and_2_out, decoder_2_out1, decoder_1_out5);
  and and_3 (and_3_out, decoder_2_out2, decoder_1_out5);
  and and_4 (and_4_out, decoder_2_out3, decoder_1_out5);
  and and_5 (and_5_out, decoder_2_out4, decoder_1_out5);
  and and_6 (and_6_out, decoder_2_out9, decoder_1_out6);
  and and_7 (and_7_out, IR[9], r);
  and and_8 (and_8_out, IR[8], r);
  and and_9 (and_9_out, IR[11], p);
  and and_10 (p, decoder_1_out3, IR[19], IR[18], decoder_2_out15);
  and and_11 (r, decoder_2_out0, decoder_1_out3, IR[19], IR[18]);
  or or_1 (Load, and_1_out, and_2_out, and_3_out, and_4_out, and_5_out, and_6_out, and_7_out, and_8_out, and_9_out);
  and and_12 (Clear, IR[13], r);
  and and_13 (Increment, IR[7], p);

  // Notes on the sheet:
  //   3x8 decoder
  //   4x8 decoder
endmodule

module AR (
  input  [19:0] Common_Bus,
  input  Clear,
  input  Load,
  input  INcrement,
  input  Clk,
  output [19:0] OUT
);

  wire or_1_out;
  wire [13:0] adder_1_out, multiplexer_1_out;

  Multiplexer #(.width(14)) multiplexer_1 (
    .in0(Common_Bus[13:0]), .in1(adder_1_out), .out(multiplexer_1_out), .sel(INcrement));  // open: en
  or or_1 (or_1_out, INcrement, Load);
  Register #(.width(14)) register_1 (.D(multiplexer_1_out), .en(or_1_out), .Q(OUT[13:0]), .clk(Clk), .clr(Clear));
  Adder #(.width(14)) adder_1 (.a(14'h1), .b(OUT[13:0]), .out(adder_1_out));  // open: cin, cout

  assign OUT[19:14] = {6{1'b0}};
endmodule

module AR_control (
  input  [19:0] IR,
  input  R,
  input  [2:0] SC,
  output Load,
  output Clear,
  output Increment
);

  wire and_1_out, and_2_out, and_3_out, decoder_1_out0, decoder_1_out1, decoder_1_out2, decoder_1_out3,
       decoder_1_out4, decoder_1_out5, decoder_1_out6, decoder_1_out7, decoder_2_out0, decoder_2_out1,
       decoder_2_out2, decoder_2_out3, decoder_2_out4, decoder_2_out5, decoder_2_out6, decoder_2_out7,
       decoder_2_out8, decoder_2_out9, decoder_2_out10, decoder_2_out11, decoder_2_out12, decoder_2_out13,
       decoder_2_out14, decoder_2_out15;

  Decoder #(.select(3)) decoder_1 (
    .out0(decoder_1_out0), .out1(decoder_1_out1), .out2(decoder_1_out2), .out3(decoder_1_out3),
    .out4(decoder_1_out4), .out5(decoder_1_out5), .out6(decoder_1_out6), .out7(decoder_1_out7), .sel(SC));  // open: en
  Decoder #(.select(4)) decoder_2 (
    .out0(decoder_2_out0), .out1(decoder_2_out1), .out2(decoder_2_out2), .out3(decoder_2_out3),
    .out4(decoder_2_out4), .out5(decoder_2_out5), .out6(decoder_2_out6), .out7(decoder_2_out7),
    .out8(decoder_2_out8), .out9(decoder_2_out9), .out10(decoder_2_out10), .out11(decoder_2_out11),
    .out12(decoder_2_out12), .out13(decoder_2_out13), .out14(decoder_2_out14), .out15(decoder_2_out15),
    .sel(IR[17:14]));  // open: en
  and and_1 (and_1_out, ~R, decoder_1_out0);  // AND_Gate
  and and_2 (and_2_out, ~decoder_2_out0, ~decoder_2_out15, decoder_1_out3, ~IR[18], ~IR[19]);  // AND_Gate
  and and_3 (and_3_out, ~R, decoder_1_out2);  // AND_Gate
  and and_4 (Clear, R, decoder_1_out1);
  and and_5 (Increment, decoder_2_out7, decoder_1_out5);
  or or_1 (Load, and_1_out, and_2_out, and_3_out);
endmodule

module DR (
  input  [19:0] CBS_Mockup,
  input  Incr,
  input  Load,
  input  in_4,
  output [19:0] out_5
);

  wire button_1_out, or_1_out;
  wire [19:0] adder_1_out, multiplexer_1_out;

  or or_1 (or_1_out, Load, Incr);
  Multiplexer #(.width(20), .enable("false")) multiplexer_1 (
    .in0(CBS_Mockup), .in1(adder_1_out), .out(multiplexer_1_out), .sel(Incr));
  Adder #(.width(20)) adder_1 (.a(20'h1), .b(out_5), .out(adder_1_out));  // open: cin, cout
  Button button_1 (.out(button_1_out));
  Register #(.width(20)) DR (.D(multiplexer_1_out), .en(or_1_out), .Q(out_5), .clk(in_4), .clr(button_1_out));
endmodule

// DR Control
module DR_control (
  input  [19:0] IR,
  input  in_2,
  output Load,
  output Increment
);

  wire and_1_out, and_2_out, and_3_out, and_4_out, button_1_out, clock_1_out, decoder_1_out0, decoder_1_out1,
       decoder_1_out2, decoder_1_out3, decoder_1_out4, decoder_1_out5, decoder_1_out6, decoder_1_out7,
       decoder_2_out0, decoder_2_out1, decoder_2_out2, decoder_2_out3, decoder_2_out4, decoder_2_out5,
       decoder_2_out6, decoder_2_out7, decoder_2_out8, decoder_2_out9, decoder_2_out10, decoder_2_out11,
       decoder_2_out12, decoder_2_out13, decoder_2_out14, decoder_2_out15;
  wire [2:0] counter_1_q;

  Counter #(.width(3), .max('h7)) counter_1 (
    .load(in_2), .Q(counter_1_q), .clk(clock_1_out), .clr(button_1_out));  // open: D, count, carry
  Clock clock_1 (.out(clock_1_out));
  Button button_1 (.out(button_1_out));
  Decoder #(.select(3)) decoder_1 (
    .out0(decoder_1_out0), .out1(decoder_1_out1), .out2(decoder_1_out2), .out3(decoder_1_out3),
    .out4(decoder_1_out4), .out5(decoder_1_out5), .out6(decoder_1_out6), .out7(decoder_1_out7),
    .sel(counter_1_q));  // open: en
  Decoder #(.select(4)) decoder_2 (
    .out0(decoder_2_out0), .out1(decoder_2_out1), .out2(decoder_2_out2), .out3(decoder_2_out3),
    .out4(decoder_2_out4), .out5(decoder_2_out5), .out6(decoder_2_out6), .out7(decoder_2_out7),
    .out8(decoder_2_out8), .out9(decoder_2_out9), .out10(decoder_2_out10), .out11(decoder_2_out11),
    .out12(decoder_2_out12), .out13(decoder_2_out13), .out14(decoder_2_out14), .out15(decoder_2_out15),
    .sel(IR[17:14]));  // open: en
  and and_1 (and_1_out, ~decoder_2_out0, ~decoder_2_out15, decoder_1_out3, ~IR[19], ~IR[18]);  // AND_Gate
  and and_2 (and_2_out, ~decoder_2_out0, ~decoder_2_out15, decoder_1_out4, ~IR[19], IR[18]);  // AND_Gate
  and and_3 (and_3_out, ~decoder_2_out0, ~decoder_2_out15, decoder_1_out3, IR[19], ~IR[18]);  // AND_Gate
  and and_4 (and_4_out, decoder_2_out9, decoder_1_out6);
  and and_5 (Increment, decoder_2_out8, decoder_1_out5);
  or or_1 (Load, and_1_out, and_2_out, and_3_out, and_4_out);
endmodule

module IR (
  input  [19:0] CBS_Mockup,
  input  Load,
  input  in_3,
  output [19:0] out_4
);

  wire button_1_out;

  Button button_1 (.out(button_1_out));
  Register #(.width(20)) IR (.D(CBS_Mockup), .en(Load), .Q(out_4), .clk(in_3), .clr(button_1_out));
endmodule

module IR_control (
  input  in_1,
  input  R,
  output Load
);

  wire button_1_out, clock_1_out, decoder_1_out0, decoder_1_out1, decoder_1_out2, decoder_1_out3,
       decoder_1_out4, decoder_1_out5, decoder_1_out6, decoder_1_out7;
  wire [2:0] counter_1_q;

  Counter #(.width(3), .max('h7)) counter_1 (
    .load(in_1), .Q(counter_1_q), .clk(clock_1_out), .clr(button_1_out));  // open: D, count, carry
  Clock clock_1 (.out(clock_1_out));
  Button button_1 (.out(button_1_out));
  Decoder #(.select(3)) decoder_1 (
    .out0(decoder_1_out0), .out1(decoder_1_out1), .out2(decoder_1_out2), .out3(decoder_1_out3),
    .out4(decoder_1_out4), .out5(decoder_1_out5), .out6(decoder_1_out6), .out7(decoder_1_out7),
    .sel(counter_1_q));  // open: en
  and and_1 (Load, ~R, decoder_1_out1);  // AND_Gate
endmodule

// Tiiming decoder
module Timing_decoder (
  input  Counter_Input,
  output out_2,
  output out_3,
  output out_4,
  output out_5,
  output out_6,
  output out_7,
  output out_8,
  output out_9
);

  wire button_1_out, clock_1_out;
  wire [2:0] counter_1_q;

  Clock clock_1 (.out(clock_1_out));
  Counter #(.width(3), .max('h7)) counter_1 (
    .load(Counter_Input), .Q(counter_1_q), .clk(clock_1_out), .clr(button_1_out));  // open: D, count, carry
  Button button_1 (.out(button_1_out));
  Decoder #(.select(3)) decoder_1 (
    .out0(out_2), .out1(out_3), .out2(out_4), .out3(out_5), .out4(out_6), .out5(out_7), .out6(out_8),
    .out7(out_9), .sel(counter_1_q));  // open: en
endmodule

// BUS Control
module Bus_Control (
  input  [19:0] IR,
  input  R,
  input  [2:0] SC,
  output [2:0] out_4
);

  wire and_1_out, and_2_out, and_3_out, and_4_out, and_5_out, and_6_out, and_7_out, and_8_out, and_9_out,
       and_10_out, and_11_out, and_12_out, and_13_out, and_14_out, and_15_out, and_17_out, and_18_out,
       and_19_out, and_20_out, and_21_out, decoder_1_out0, decoder_1_out1, decoder_1_out2, decoder_1_out3,
       decoder_1_out4, decoder_1_out5, decoder_1_out6, decoder_1_out7, decoder_2_out0, decoder_2_out1,
       decoder_2_out2, decoder_2_out3, decoder_2_out4, decoder_2_out5, decoder_2_out6, decoder_2_out7,
       decoder_2_out8, decoder_2_out9, decoder_2_out10, decoder_2_out11, decoder_2_out12, decoder_2_out13,
       decoder_2_out14, decoder_2_out15, or_1_out, or_2_out, or_3_out, or_4_out, or_5_out, or_6_out, p;

  Decoder #(.select(3)) decoder_1 (
    .out0(decoder_1_out0), .out1(decoder_1_out1), .out2(decoder_1_out2), .out3(decoder_1_out3),
    .out4(decoder_1_out4), .out5(decoder_1_out5), .out6(decoder_1_out6), .out7(decoder_1_out7), .sel(SC));  // open: en
  Decoder #(.select(4)) decoder_2 (
    .out0(decoder_2_out0), .out1(decoder_2_out1), .out2(decoder_2_out2), .out3(decoder_2_out3),
    .out4(decoder_2_out4), .out5(decoder_2_out5), .out6(decoder_2_out6), .out7(decoder_2_out7),
    .out8(decoder_2_out8), .out9(decoder_2_out9), .out10(decoder_2_out10), .out11(decoder_2_out11),
    .out12(decoder_2_out12), .out13(decoder_2_out13), .out14(decoder_2_out14), .out15(decoder_2_out15),
    .sel(IR[17:14]));  // open: en
  and and_1 (and_1_out, decoder_2_out6, decoder_1_out5);
  and and_2 (and_2_out, decoder_2_out7, decoder_1_out6);
  and and_3 (and_3_out, R, decoder_1_out0);
  and and_4 (and_4_out, R, decoder_1_out1);
  and and_5 (and_5_out, decoder_2_out7, decoder_1_out5);
  and and_6 (and_6_out, decoder_2_out4, decoder_1_out5);
  and and_7 (and_7_out, decoder_2_out8, decoder_1_out6);
  and and_8 (and_8_out, decoder_2_out9, decoder_1_out6);
  and and_9 (and_9_out, decoder_2_out5, decoder_1_out5);
  and and_10 (and_10_out, decoder_2_out9, decoder_1_out5);
  and and_11 (and_11_out, IR[12], p);
  and and_12 (and_12_out, ~R, decoder_1_out2);  // AND_Gate
  and and_13 (and_13_out, R, decoder_1_out2);
  and and_14 (and_14_out, decoder_2_out9, decoder_1_out6);
  and and_15 (and_15_out, ~R, decoder_1_out1);  // AND_Gate
  and and_16 (p, decoder_1_out3, IR[19], IR[18], decoder_2_out15);
  and and_17 (and_17_out, ~decoder_2_out0, ~decoder_2_out15, decoder_1_out3, IR[19], ~IR[18]);  // AND_Gate
  and and_18 (and_18_out, ~decoder_2_out0, ~decoder_2_out15, decoder_1_out3, ~IR[19], ~IR[18]);  // AND_Gate
  and and_19 (and_19_out, ~decoder_2_out0, ~decoder_2_out15, decoder_1_out3, ~IR[19], IR[18]);  // AND_Gate
  and and_20 (and_20_out, ~decoder_2_out0, ~decoder_2_out15, decoder_1_out4, ~IR[19], IR[18]);  // AND_Gate
  or or_1 (or_1_out, and_6_out, and_7_out, and_8_out);
  or or_2 (or_2_out, and_9_out, and_10_out, and_11_out);
  or or_3 (or_3_out, and_13_out, and_14_out);
  or or_4 (or_4_out, and_17_out, and_1_out, and_2_out);
  or or_5 (or_5_out, and_3_out, and_4_out, and_5_out);
  and and_21 (and_21_out, ~or_4_out, ~or_5_out, ~or_1_out, ~or_2_out, ~and_12_out, ~or_3_out, ~or_6_out);  // AND_Gate
  or or_6 (or_6_out, and_15_out, and_18_out, and_19_out, and_20_out);
  Priority_Encoder priority_encoder_1 (
    .in0(and_21_out), .in1(or_4_out), .in2(or_5_out), .in3(or_1_out), .in4(or_2_out), .in5(and_12_out),
    .in6(or_3_out), .in7(or_6_out), .out(out_4));  // open: en_in, gs, en_out
endmodule

module Final (
  input  [19:0] IR,
  input  in_2
);

  wire ac_control_1_clear, ac_control_1_increment, ac_control_1_load, ar_control_1_clear,
       ar_control_1_increment, ar_control_1_load, dr_control_1_increment, ir_control_1_load,
       pc_control_1_clear, pc_control_1_increment, pc_control_1_load;
  wire [2:0] undriven, undriven_6;
  wire [19:0] ac_1_out_6, and_1_out, ar_1_out, dr_1_out_5, ir_1_out_4, memory_1_output, multiplexer_1_out,
       pc_1_out, undriven_2, undriven_3, undriven_4, undriven_5, undriven_7, undriven_8;

  assign and_1_out = undriven_4 & undriven_3 & undriven_2;  // AND_Gate and_1, 20 bits wide
  Memory_Control memory_control_1 ();  // open: R, IR, Write, SC
  Memory memory_1 (
    .AR(ar_1_out), .Output(memory_1_output), .CBS_Mockup(multiplexer_1_out));  // open: IR, SC, R, Read, in_6
  AR_control ar_control_1 (
    .Load(ar_control_1_load), .Clear(ar_control_1_clear), .Increment(ar_control_1_increment), .R(in_2),
    .IR(undriven_5), .SC(undriven));
  PC_control pc_control_1 (
    .Load(pc_control_1_load), .Increment(pc_control_1_increment), .Clear(pc_control_1_clear));  // open: IR, SC, R, FGI, FGO, E, AC, DR
  DR_control dr_control_1 (.Increment(dr_control_1_increment));  // open: IR, in_2, Load
  DR dr_1 (.out_5(dr_1_out_5), .CBS_Mockup(multiplexer_1_out));  // open: in_4, Incr, Load
  AC_control ac_control_1 (
    .Clear(ac_control_1_clear), .Increment(ac_control_1_increment), .Load(ac_control_1_load));  // open: SC, IR
  AC ac_1 (
    .out_6(ac_1_out_6), .Incr(ac_control_1_increment), .Load(ac_control_1_load), .Clear(ac_control_1_clear));  // open: in_5, ALU
  IR_control ir_control_1 (.Load(ir_control_1_load));  // open: in_1, R
  IR ir_1 (.Load(ir_control_1_load), .out_4(ir_1_out_4), .CBS_Mockup(multiplexer_1_out));  // open: in_3
  Bus_Control bus_control_1 ();  // open: SC, IR, R, out_4
  AR ar_1 (
    .OUT(ar_1_out), .Load(ar_control_1_increment), .Clear(ar_control_1_clear), .INcrement(ar_control_1_load),
    .Common_Bus(multiplexer_1_out));  // open: Clk
  PC pc_1 (
    .Common_Bus(multiplexer_1_out), .OUT(pc_1_out), .in_2(pc_control_1_clear), .in_3(pc_control_1_load),
    .in_4(pc_control_1_increment));  // open: in_5
  Multiplexer #(.select(3), .width(20), .enable("false")) multiplexer_1 (
    .in0(undriven_7), .in1(ar_1_out), .in2(pc_1_out), .in3(dr_1_out_5), .in4(ac_1_out_6), .in5(ir_1_out_4),
    .in6(undriven_8), .in7(memory_1_output), .out(multiplexer_1_out), .sel(undriven_6));

  // Notes on the sheet:
  //   Common Bus
endmodule

module Memory (
  input  [19:0] AR,
  input  [19:0] IR,
  input  [19:0] CBS_Mockup,
  input  [2:0] SC,
  input  R,
  input  in_6,
  input  Read,
  output [19:0] Output
);

  wire memory_control_1_write;

  Memory_Control memory_control_1 (.R(R), .IR(IR), .Write(memory_control_1_write), .SC(SC));
  RAM #(.addrWidth(14), .dataWidth(20), .bus("separate")) ram_1 (
    .addr(AR[13:0]), .din(CBS_Mockup), .data(Output), .str(memory_control_1_write), .clk(in_6), .ld(Read));  // open: sel, clr

  // Notes on the sheet:
  //   Write
endmodule

module Memory_Control (
  input  [19:0] IR,
  input  [2:0] SC,
  input  R,
  output Write
);

  wire and_1_out, and_2_out, and_3_out, and_4_out, decoder_1_out0, decoder_1_out1, decoder_1_out2,
       decoder_1_out3, decoder_1_out4, decoder_1_out5, decoder_1_out6, decoder_1_out7, decoder_2_out0,
       decoder_2_out1, decoder_2_out2, decoder_2_out3, decoder_2_out4, decoder_2_out5, decoder_2_out6,
       decoder_2_out7, decoder_2_out8, decoder_2_out9, decoder_2_out10, decoder_2_out11, decoder_2_out12,
       decoder_2_out13, decoder_2_out14, decoder_2_out15;

  Decoder #(.select(3), .enable("false")) decoder_1 (
    .out0(decoder_1_out0), .out1(decoder_1_out1), .out2(decoder_1_out2), .out3(decoder_1_out3),
    .out4(decoder_1_out4), .out5(decoder_1_out5), .out6(decoder_1_out6), .out7(decoder_1_out7), .sel(SC));
  Decoder #(.select(4), .enable("false")) decoder_2 (
    .out0(decoder_2_out0), .out1(decoder_2_out1), .out2(decoder_2_out2), .out3(decoder_2_out3),
    .out4(decoder_2_out4), .out5(decoder_2_out5), .out6(decoder_2_out6), .out7(decoder_2_out7),
    .out8(decoder_2_out8), .out9(decoder_2_out9), .out10(decoder_2_out10), .out11(decoder_2_out11),
    .out12(decoder_2_out12), .out13(decoder_2_out13), .out14(decoder_2_out14), .out15(decoder_2_out15),
    .sel(IR[17:14]));
  and and_1 (and_1_out, R, decoder_1_out2);
  and and_2 (and_2_out, decoder_1_out5, decoder_2_out5);
  and and_3 (and_3_out, decoder_1_out5, decoder_2_out7);
  and and_4 (and_4_out, decoder_2_out8, decoder_1_out6);
  or or_1 (Write, and_1_out, and_2_out, and_3_out, and_4_out);
endmodule

module pc_KO_LAGI (
  input  [19:0] AC,
  input  [19:0] DR,
  input  FGO,
  input  FGI,
  input  R,
  input  E,
  input  [2:0] in_7
);

  wire [19:0] undriven;

  PC_control pc_control_1 (
    .IR(undriven), .SC(in_7), .R(R), .FGI(FGI), .FGO(FGO), .E(E), .AC(AC), .DR(DR));  // open: Load, Increment, Clear
endmodule

module shift (
  input  [19:0] in_1,
  input  [4:0] in_2,
  output [19:0] out_3
);

  Shifter #(.width(20)) shifter_1 (.in(in_1), .\dist (in_2), .out(out_3));
endmodule
